# Fritzing sketch Multimeter_Schematic (1) (saved by Fritzing 0.9.3b)

parts:
  R1 = Resistor [tolerance=±5% resistance=2 package="2010 [SMD]"]
  R2 = Resistor [tolerance=±5% resistance=4.7k package="2010 [SMD]"]
  R3 = Resistor [tolerance=±5% resistance=0 package="1206 [SMD]"]
  R6 = Resistor [tolerance=±5% resistance=1k package="1206 [SMD]"]
  R4 = Resistor [tolerance=±5% resistance=100k package="1206 [SMD]"]
  R5 = Resistor [tolerance=±5% resistance=10k package="1206 [SMD]"]
  J1 = Piezo Speaker
  LED2 = LED - 5mm [color="Red (633nm)" package="5 mm [THT]"]
  TRRS1 = Audio Jack (TRRS) 3.5mm [part_number="LUMBERG JEITA RC-5325A" package="RC-5325A [SMD]"]
  Part1 = Arduino Uno (Rev3)
  U1 = ESP32-38PinWide [part_number=ESP32-38PinWide]

nets:
  N1: R1.Pin_0, R3.Pin_0, R6.Pin_1, R4.Pin_1, R5.Pin_1, J1.pin2, LED2.cathode, Part1.A0
  N2: R1.Pin_1, R2.Pin_0, Part1.A2
  N3: R2.Pin_1, R3.Pin_1, J1.pin1, LED2.anode, TRRS1.SLEEVE
  N4: R6.Pin_0, Part1.D5_PWM
  N5: R4.Pin_0, Part1.D6_PWM
  N6: R5.Pin_0, Part1.D4
  N7: Part1.D8, U1.GPIO17
  N8: Part1.D12/MISO, U1.GPIO16
  GND: Part1.GND, U1.GND
  5V: Part1.5V, U1.VIN

custom parts:
  ESP32-38PinWide: Generic 38-Pin ESP32 with wide format (only access to one side of pins on a breadboard) based on Stephen Lilley's HiLetgo ESP-WROOM-32 ESP32 ESP-32S Development Board.
