# Fritzing sketch Multimeter_Schematic (saved by Fritzing 0.9.3b)

parts:
  U1 = ESP32-38PinWide [part_number=ESP32-38PinWide]
  R1 = Resistor [tolerance=±5% resistance=2 package="2010 [SMD]"]
  R2 = Resistor [tolerance=±5% resistance=4.7k package="2010 [SMD]"]
  Part1 = Current Sensor 5A
  RE1 = Rotary Encoder [package=THT]
  R3 = Resistor [tolerance=±5% resistance=0 package="1206 [SMD]"]
  R6 = Resistor [tolerance=±5% resistance=1k package="1206 [SMD]"]
  Part2 = Logic Level Converter
  Part3 = Adafruit Micro USB Breakout [part_number="Adafruit #1833"]
  OLED_I2C1 = OLED 128x64 I2C Monochrome Display
  R4 = Resistor [tolerance=±5% resistance=100k package="1206 [SMD]"]
  R5 = Resistor [tolerance=±5% resistance=10k package="1206 [SMD]"]
  J1 = Piezo Speaker
  LED1 = LED - 5mm [color="Red (633nm)" package="5 mm [THT]"]
  LED2 = LED - 5mm [color="Red (633nm)" package="5 mm [THT]"]
  LED3 = LED - 5mm [color="Red (633nm)" package="5 mm [THT]"]

nets:
  N1: U1.3.3, RE1.EncoderPinB, Part2.LV
  N2: U1.GPIO39, U1.GPIO34, R5.Pin_0
  N3: U1.GPIO35, R4.Pin_0
  N4: U1.GPIO32, R6.Pin_0
  N5: U1.GPIO33, U1.GPIO25, R1.Pin_1, R2.Pin_0
  N6: U1.GND, RE1.EncoderPinA, R3.Pin_1, J1.pin1, LED2.anode
  GND: U1.GPIO11, R2.Pin_1, Part1.GND, Part2.GND, Part3.GND, OLED_I2C1.GND, LED1.anode
  VIN: U1.VIN, Part1.VCC, Part2.HV, Part3.VBUS, OLED_I2C1.VDD
  N7: U1.GPIO15, R3.Pin_0, R6.Pin_1, R4.Pin_1, R5.Pin_1, LED2.cathode
  N8: U1.GPIO2, RE1.EncoderPinC
  N9: U1.GPIO0, Part2.RX2_LV
  N10: U1.GPIO17, J1.pin2
  N11: U1.GPIO21, Part2.TX_LV
  N12: U1.GPIO22, Part2.RX_LV
  N13: R1.Pin_0, LED1.cathode
  N14: Part1.1, LED3.anode
  N15: Part1.2, Part1.OUT, Part2.RX2_HV, LED3.cathode
  N16: Part2.TX_HV, OLED_I2C1.SDA
  N17: Part2.RX_HV, OLED_I2C1.SCK

custom parts:
  ESP32-38PinWide: Generic 38-Pin ESP32 with wide format (only access to one side of pins on a breadboard) based on Stephen Lilley's HiLetgo ESP-WROOM-32 ESP32 ESP-32S Development Board.
  Adafruit Micro USB Breakout: Simple but effective - this breakout board has a USB Micro-B connector, with all 5 pins broken out. Great for pairing with a microcontroller with USB support, or adding USB 5V power to a project. We use a micro-AB connector with through-hole shielding pads for an excellent strong connection - it won't rip off by accident! Comes with one fully assembled and tested micro B breakout PCB and a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
